// Digital circuit New_Address_Decode.dig as structural Verilog
module New_Address_Decode (
  input  A0,
  input  A1,
  input  A2,
  input  A3,
  input  A4,
  input  A5,
  input  A6,
  input  A7,
  input  A8,
  input  A9,
  input  A10,
  input  A11,
  input  A12,
  input  R_nW,
  input  AS,
  output nQ0,
  output RAM_2_nCE,
  output nQ4,
  output nQ5,
  output nQ6,
  output nQ7,
  output ROM_nCE
);

  wire _74138_1_pin12, _74138_1_pin13;

  _74138 _74138_1 (
    .pin1(A11), .pin2(A12), .pin3(1'b0), .pin4(1'b0), .pin5(1'b0), .pin6(AS), .pin7(nQ7), .pin8(1'b0),
    .pin9(nQ6), .pin10(nQ5), .pin11(nQ4), .pin12(_74138_1_pin12), .pin13(_74138_1_pin13), .pin14(RAM_2_nCE),
    .pin15(nQ0), .pin16(1'b1));
  and and_1 (ROM_nCE, _74138_1_pin13, _74138_1_pin12);

  // Notes on the sheet:
  //   R_nW: Read High, Write Low
  //   AS: Address Select
  //   nQ0: RAM 1 ~CE driver
  //   RAM_2_nCE: RAM 2 ~CE
endmodule
